// Logisim project main.circ as structural Verilog: 13 circuits, main circuit main
module main (
  input  [3:0] in_1,
  input  OE,
  input  [7:0] TD,
  input  OETD,
  input  CountE,
  output [3:0] Cntr_Content,
  output [7:0] IR_Content,
  output [3:0] MAR_Content,
  output [7:0] MBR_Reg_Content,
  output [7:0] Reg_A_Content,
  output [7:0] ALU_Result,
  output [7:0] O_P_Reg_Content,
  output [7:0] Reg_B_Content
);

  wire clock_out, cu_1_1_c0, cu_1_1_c1, cu_1_1_c2, cu_1_1_c3, cu_1_1_c4, cu_1_1_c5, cu_1_1_c6, cu_1_1_c7,
       cu_1_1_c8, cu_1_1_c9, cu_1_1_c10, cu_1_1_c11, cu_2_1_c12, cu_2_1_c13, cu_2_1_c14, cu_2_1_c15;
  wire [2:0] PC_2_q, undriven;
  wire [3:0] bitselector_1_out, controlled_buffer_1_out, decimal_decoer_2_dout_2, decimal_decoer_2_dout_3,
       decimal_decoer_3_dout_2, decimal_decoer_3_dout_3, decimal_decoer_4_dout_2, decimal_decoer_4_dout_3,
       mar_1_dout;
  wire [7:0] alu_1_dout, bit_extender_1_out, bit_extender_2_out, decimal_decoer_2_dout,
       decimal_decoer_3_dout, decimal_decoer_4_dout, IR_dout, ram_1_dout;
  wire [15:0] decimal_decoer_2_dout_4, decimal_decoer_3_dout_4, decimal_decoer_4_dout_4;
  wire [31:0] decimal_decoer_1_dout, decimal_decoer_5_dout;

  _7_Segment_Display u_7_segment_display_1 (
    .g(decimal_decoer_2_dout_3[3]), .f(decimal_decoer_2_dout_3[2]), .a(decimal_decoer_2_dout_3[1]),
    .b(decimal_decoer_2_dout_3[0]), .e(decimal_decoer_2_dout_4[15]), .d(decimal_decoer_2_dout_4[14]),
    .c(decimal_decoer_2_dout_4[13]), .dp(decimal_decoer_2_dout_4[12]));
  _7_Segment_Display u_7_segment_display_2 (
    .g(decimal_decoer_2_dout_2[3]), .f(decimal_decoer_2_dout_2[2]), .a(decimal_decoer_2_dout_2[1]),
    .b(decimal_decoer_2_dout_2[0]), .e(decimal_decoer_2_dout_4[11]), .d(decimal_decoer_2_dout_4[10]),
    .c(decimal_decoer_2_dout_4[9]), .dp(decimal_decoer_2_dout_4[8]));
  _7_Segment_Display u_7_segment_display_3 (
    .g(decimal_decoer_2_dout[7]), .f(decimal_decoer_2_dout[6]), .a(decimal_decoer_2_dout[5]),
    .b(decimal_decoer_2_dout[4]), .e(decimal_decoer_2_dout_4[7]), .d(decimal_decoer_2_dout_4[6]),
    .c(decimal_decoer_2_dout_4[5]), .dp(decimal_decoer_2_dout_4[4]));
  assign bit_extender_1_out = {{4{1'b0}}, Cntr_Content};  // Bit_Extender bit_extender_1
  Decimal_Decoer decimal_decoer_1 (.Din(bit_extender_1_out), .Dout(decimal_decoer_1_dout));
  _7_Segment_Display u_7_segment_display_4 (
    .g(decimal_decoer_1_dout[3]), .f(decimal_decoer_1_dout[2]), .a(decimal_decoer_1_dout[1]),
    .b(decimal_decoer_1_dout[0]), .e(decimal_decoer_1_dout[19]), .d(decimal_decoer_1_dout[18]),
    .c(decimal_decoer_1_dout[17]), .dp(decimal_decoer_1_dout[16]));
  Decimal_Decoer decimal_decoer_2 (
    .Din(Reg_A_Content),
    .Dout({decimal_decoer_2_dout_4, decimal_decoer_2_dout_3, decimal_decoer_2_dout_2, decimal_decoer_2_dout}));
  _7_Segment_Display u_7_segment_display_5 (
    .g(decimal_decoer_2_dout[3]), .f(decimal_decoer_2_dout[2]), .a(decimal_decoer_2_dout[1]),
    .b(decimal_decoer_2_dout[0]), .e(decimal_decoer_2_dout_4[3]), .d(decimal_decoer_2_dout_4[2]),
    .c(decimal_decoer_2_dout_4[1]), .dp(decimal_decoer_2_dout_4[0]));
  Clock clock (.out(clock_out));
  Counter #(.max('h3), .width(4)) PC (
    .D(controlled_buffer_1_out), .count(cu_1_1_c1), .Q(Cntr_Content), .clk(clock_out));  // open: load, carry, clr
  Register IR (
    .clock(clock_out), .WE(cu_1_1_c7), .Din(alu_1_dout), .OE(cu_1_1_c8), .Dout(IR_dout),
    .Stored_Data(IR_Content));
  Register Reg_A (.clock(clock_out), .WE(cu_2_1_c12), .Din(alu_1_dout), .Stored_Data(Reg_A_Content));  // open: OE, Dout
  ALU alu_1 (
    .OE(cu_1_1_c11), .Reg_A(Reg_A_Content), .Reg_B(Reg_B_Content), .Dout(alu_1_dout), .ALU_result(ALU_Result));  // open: Carry_out
  Register Reg_B (.clock(clock_out), .WE(cu_2_1_c13), .Din(alu_1_dout), .Stored_Data(Reg_B_Content));  // open: OE, Dout
  _7_Segment_Display u_7_segment_display_6 (
    .g(decimal_decoer_3_dout_3[3]), .f(decimal_decoer_3_dout_3[2]), .a(decimal_decoer_3_dout_3[1]),
    .b(decimal_decoer_3_dout_3[0]), .e(decimal_decoer_3_dout_4[15]), .d(decimal_decoer_3_dout_4[14]),
    .c(decimal_decoer_3_dout_4[13]), .dp(decimal_decoer_3_dout_4[12]));
  _7_Segment_Display u_7_segment_display_7 (
    .g(decimal_decoer_3_dout_2[3]), .f(decimal_decoer_3_dout_2[2]), .a(decimal_decoer_3_dout_2[1]),
    .b(decimal_decoer_3_dout_2[0]), .e(decimal_decoer_3_dout_4[11]), .d(decimal_decoer_3_dout_4[10]),
    .c(decimal_decoer_3_dout_4[9]), .dp(decimal_decoer_3_dout_4[8]));
  assign controlled_buffer_1_out = cu_1_1_c0 ? Cntr_Content : 4'bz;  // Controlled_Buffer controlled_buffer_1
  Decimal_Decoer decimal_decoer_3 (
    .Din(Reg_B_Content),
    .Dout({decimal_decoer_3_dout_4, decimal_decoer_3_dout_3, decimal_decoer_3_dout_2, decimal_decoer_3_dout}));
  _7_Segment_Display u_7_segment_display_8 (
    .g(decimal_decoer_3_dout[7]), .f(decimal_decoer_3_dout[6]), .a(decimal_decoer_3_dout[5]),
    .b(decimal_decoer_3_dout[4]), .e(decimal_decoer_3_dout_4[7]), .d(decimal_decoer_3_dout_4[6]),
    .c(decimal_decoer_3_dout_4[5]), .dp(decimal_decoer_3_dout_4[4]));
  _7_Segment_Display u_7_segment_display_9 (
    .g(decimal_decoer_3_dout[3]), .f(decimal_decoer_3_dout[2]), .a(decimal_decoer_3_dout[1]),
    .b(decimal_decoer_3_dout[0]), .e(decimal_decoer_3_dout_4[3]), .d(decimal_decoer_3_dout_4[2]),
    .c(decimal_decoer_3_dout_4[1]), .dp(decimal_decoer_3_dout_4[0]));
  BitSelector #(.group(4)) bitselector_1 (.in(IR_dout), .out(bitselector_1_out), .sel(1'b1));
  BitSelector #(.group(4)) bitselector_2 (.in(IR_dout), .out(controlled_buffer_1_out), .sel(1'b0));
  LED D7 (.in(alu_1_dout[7]));
  assign alu_1_dout = OETD ? TD : 8'bz;  // Controlled_Buffer controlled_buffer_2
  LED D6 (.in(alu_1_dout[6]));
  LED D5 (.in(alu_1_dout[5]));
  LED D4 (.in(alu_1_dout[4]));
  LED D3 (.in(alu_1_dout[3]));
  assign alu_1_dout = cu_1_1_c5 ? MBR_Reg_Content : 8'bz;  // Controlled_Buffer controlled_buffer_3
  _7_Segment_Display u_7_segment_display_10 (
    .g(decimal_decoer_4_dout_3[3]), .f(decimal_decoer_4_dout_3[2]), .a(decimal_decoer_4_dout_3[1]),
    .b(decimal_decoer_4_dout_3[0]), .e(decimal_decoer_4_dout_4[15]), .d(decimal_decoer_4_dout_4[14]),
    .c(decimal_decoer_4_dout_4[13]), .dp(decimal_decoer_4_dout_4[12]));
  LED D2 (.in(alu_1_dout[2]));
  LED D1 (.in(alu_1_dout[1]));
  LED D0 (.in(alu_1_dout[0]));
  _7_Segment_Display u_7_segment_display_11 (
    .g(decimal_decoer_4_dout_2[3]), .f(decimal_decoer_4_dout_2[2]), .a(decimal_decoer_4_dout_2[1]),
    .b(decimal_decoer_4_dout_2[0]), .e(decimal_decoer_4_dout_4[11]), .d(decimal_decoer_4_dout_4[10]),
    .c(decimal_decoer_4_dout_4[9]), .dp(decimal_decoer_4_dout_4[8]));
  _7_Segment_Display u_7_segment_display_12 (
    .g(decimal_decoer_4_dout[7]), .f(decimal_decoer_4_dout[6]), .a(decimal_decoer_4_dout[5]),
    .b(decimal_decoer_4_dout[4]), .e(decimal_decoer_4_dout_4[7]), .d(decimal_decoer_4_dout_4[6]),
    .c(decimal_decoer_4_dout_4[5]), .dp(decimal_decoer_4_dout_4[4]));
  MAR mar_1 (
    .clock(clock_out), .WE(cu_1_1_c9), .Din(controlled_buffer_1_out), .OE(cu_1_1_c10), .Dout(mar_1_dout),
    .Stored_Data(MAR_Content));
  Register MBR (
    .clock(clock_out), .WE(cu_1_1_c4), .Din(alu_1_dout), .OE(cu_1_1_c6), .Dout(alu_1_dout),
    .Stored_Data(MBR_Reg_Content));
  Register O_P_Reg (
    .clock(clock_out), .WE(cu_2_1_c15), .Din(alu_1_dout), .OE(cu_2_1_c14), .Dout(alu_1_dout),
    .Stored_Data(O_P_Reg_Content));
  Decimal_Decoer decimal_decoer_4 (
    .Din(O_P_Reg_Content),
    .Dout({decimal_decoer_4_dout_4, decimal_decoer_4_dout_3, decimal_decoer_4_dout_2, decimal_decoer_4_dout}));
  _7_Segment_Display u_7_segment_display_13 (
    .g(decimal_decoer_4_dout[3]), .f(decimal_decoer_4_dout[2]), .a(decimal_decoer_4_dout[1]),
    .b(decimal_decoer_4_dout[0]), .e(decimal_decoer_4_dout_4[3]), .d(decimal_decoer_4_dout_4[2]),
    .c(decimal_decoer_4_dout_4[1]), .dp(decimal_decoer_4_dout_4[0]));
  assign mar_1_dout = OE ? in_1 : 4'bz;  // Controlled_Buffer controlled_buffer_4
  LED D7_2 (.in(alu_1_dout[7]));
  LED D6_2 (.in(alu_1_dout[6]));
  LED D5_2 (.in(alu_1_dout[5]));
  LED D4_2 (.in(alu_1_dout[4]));
  LED D3_2 (.in(alu_1_dout[3]));
  RAM #(.addrWidth(4)) ram_1 (.addr(mar_1_dout), .we(cu_1_1_c2), .clk(clock_out), .din(alu_1_dout), .dout(ram_1_dout));
  LED D2_2 (.in(alu_1_dout[2]));
  LED D1_2 (.in(alu_1_dout[1]));
  LED D0_2 (.in(alu_1_dout[0]));
  Decimal_Decoer decimal_decoer_5 (.Din(bit_extender_2_out), .Dout(decimal_decoer_5_dout));
  _7_Segment_Display u_7_segment_display_14 (
    .g(decimal_decoer_5_dout[3]), .f(decimal_decoer_5_dout[2]), .a(decimal_decoer_5_dout[1]),
    .b(decimal_decoer_5_dout[0]), .e(decimal_decoer_5_dout[19]), .d(decimal_decoer_5_dout[18]),
    .c(decimal_decoer_5_dout[17]), .dp(decimal_decoer_5_dout[16]));
  assign alu_1_dout = cu_1_1_c3 ? ram_1_dout : 8'bz;  // Controlled_Buffer controlled_buffer_5
  CU_1 cu_1_1 (
    .OPC3(bitselector_1_out[3]), .OPC2(bitselector_1_out[2]), .OPC1(bitselector_1_out[1]),
    .OPC0(bitselector_1_out[0]), .SC2(PC_2_q[2]), .SC1(PC_2_q[1]), .SC0(PC_2_q[0]), .C0(cu_1_1_c0),
    .C1(cu_1_1_c1), .C2(cu_1_1_c2), .C3(cu_1_1_c3), .C4(cu_1_1_c4), .C5(cu_1_1_c5), .C6(cu_1_1_c6),
    .C7(cu_1_1_c7), .C8(cu_1_1_c8), .C9(cu_1_1_c9), .C10(cu_1_1_c10), .C11(cu_1_1_c11));
  CU_2 cu_2_1 (
    .OPC3(bitselector_1_out[3]), .OPC2(bitselector_1_out[2]), .OPC1(bitselector_1_out[1]),
    .OPC0(bitselector_1_out[0]), .SC2(PC_2_q[2]), .SC1(PC_2_q[1]), .SC0(PC_2_q[0]), .C12(cu_2_1_c12),
    .C13(cu_2_1_c13), .C14(cu_2_1_c14), .C15(cu_2_1_c15));
  assign bit_extender_2_out = {{5{1'b0}}, PC_2_q};  // Bit_Extender bit_extender_2
  Counter #(.max('h5), .width(3)) PC_2 (
    .D(undriven), .count(CountE), .Q(PC_2_q), .clk(clock_out));  // open: load, carry, clr

  // Notes on the sheet:
  //   OETD-OE Testing Data 
  //   TD-Testing Data 
  //   Internal Address Bus(4 bits)
  //   Internal Data Bus
  //   External 
  //   Address 
  //   Bus(4 bits)
  //   External Data Bus
endmodule

module Memory_Cell (
  input  clock,
  input  WE,
  input  Din,
  input  OE,
  input  Reset,
  output Dout,
  output Stored_Data
);

  wire and_1_out, and_2_out, not_1_out, or_1_out;

  not not_1 (not_1_out, WE);
  and and_1 (and_1_out, Stored_Data, not_1_out);
  and and_2 (and_2_out, WE, Din);
  or or_1 (or_1_out, and_1_out, and_2_out);
  D_Flip_Flop #(.enable("true")) d_ff_1 (
    .clk(clock), .D(or_1_out), .Q(Stored_Data), .reset(Reset));  // open: Qn, preset, en
  assign Dout = OE ? Stored_Data : 1'bz;  // Controlled_Buffer controlled_buffer_1

  // Notes on the sheet:
  //   Din-Data in
  //   Memory Cell(1 bit)
  //   WE-write_enable
  //   OE- output enable pin
  //   Dout-stored data goes out to the bus
endmodule

module Register (
  input  clock,
  input  WE,
  input  [7:0] Din,
  input  OE,
  output [7:0] Dout,
  output [7:0] Stored_Data
);

  Memory_Cell _0 (
    .clock(clock), .WE(WE), .Din(Din[0]), .OE(OE), .Dout(Dout[0]), .Stored_Data(Stored_Data[0]));  // open: Reset
  Memory_Cell _1 (
    .clock(clock), .WE(WE), .Din(Din[1]), .OE(OE), .Dout(Dout[1]), .Stored_Data(Stored_Data[1]));  // open: Reset
  Memory_Cell _2 (
    .clock(clock), .WE(WE), .Din(Din[2]), .OE(OE), .Dout(Dout[2]), .Stored_Data(Stored_Data[2]));  // open: Reset
  Memory_Cell _3 (
    .clock(clock), .WE(WE), .Din(Din[3]), .OE(OE), .Dout(Dout[3]), .Stored_Data(Stored_Data[3]));  // open: Reset
  Memory_Cell _4 (
    .clock(clock), .WE(WE), .Din(Din[4]), .OE(OE), .Dout(Dout[4]), .Stored_Data(Stored_Data[4]));  // open: Reset
  Memory_Cell _5 (
    .clock(clock), .WE(WE), .Din(Din[5]), .OE(OE), .Dout(Dout[5]), .Stored_Data(Stored_Data[5]));  // open: Reset
  Memory_Cell _6 (
    .clock(clock), .WE(WE), .Din(Din[6]), .OE(OE), .Dout(Dout[6]), .Stored_Data(Stored_Data[6]));  // open: Reset
  Memory_Cell _7 (
    .clock(clock), .WE(WE), .Din(Din[7]), .OE(OE), .Dout(Dout[7]), .Stored_Data(Stored_Data[7]));  // open: Reset

  // Notes on the sheet:
  //   Register (8 bits)
endmodule

module MAR (
  input  clock,
  input  WE,
  input  [3:0] Din,
  input  OE,
  output [3:0] Dout,
  output [3:0] Stored_Data
);

  Memory_Cell _0 (
    .clock(clock), .WE(WE), .Din(Din[0]), .OE(OE), .Dout(Dout[0]), .Stored_Data(Stored_Data[0]));  // open: Reset
  Memory_Cell _1 (
    .clock(clock), .WE(WE), .Din(Din[1]), .OE(OE), .Dout(Dout[1]), .Stored_Data(Stored_Data[1]));  // open: Reset
  Memory_Cell _2 (
    .clock(clock), .WE(WE), .Din(Din[2]), .OE(OE), .Dout(Dout[2]), .Stored_Data(Stored_Data[2]));  // open: Reset
  Memory_Cell _3 (
    .clock(clock), .WE(WE), .Din(Din[3]), .OE(OE), .Dout(Dout[3]), .Stored_Data(Stored_Data[3]));  // open: Reset

  // Notes on the sheet:
  //   MAR (4 bits)
endmodule

module ALU (
  input  OE,
  input  [7:0] Reg_A,
  input  [7:0] Reg_B,
  output [7:0] Dout,
  output [7:0] ALU_result,
  output Carry_out
);

  Adder adder_1 (.a(Reg_A), .b(Reg_B), .out(ALU_result), .cout(Carry_out));  // open: cin
  assign Dout = OE ? ALU_result : 8'bz;  // Controlled_Buffer controlled_buffer_1

  // Notes on the sheet:
  //   ALU(8 bits)
endmodule

module Decimal_Decoer (
  input  [7:0] Din,
  output [31:0] Dout
);

  ROM #(.dataWidth(32)) rom_1 (
    .addr(Din),
    .data({Dout[31:28], Dout[15:12], Dout[27:24], Dout[11:8], Dout[23:20], Dout[7:4], Dout[19:16], Dout[3:0]}));

  // Notes on the sheet:
  //   Decimal Decoder
  //   contents of rom_1 (hex, n*v repeats v):
  //   e7 21 cb 6b 2d 6e ee 23 ef 2f 21e7 2121 21cb 216b 212d 216e 21ee 2123 21ef 212f cbe7 cb21 cbcb cb6b
  //   cb2d cb6e cbee cb23 cbef cb2f 6be7 6b21 6bcb 6b6b 6b2d 6b6e 6bee 6b23 6bef 6b2f 2de7 2d21 2dcb 2d6b
  //   2d2d 2d6e 2dee 2d23 2def 2d2f 6ee7 6e21 6ecb 6e6b 6e2d 6e6e 6eee 6e23 6eef 6e2f eee7 ee21 eecb ee6b
  //   ee2d ee6e eeee ee23 eeef ee2f 23e7 2321 23cb 236b 232d 236e 23ee 2323 23ef 232f efe7 ef21 efcb ef6b
  //   ef2d ef6e efee ef23 efef ef2f 2fe7 2f21 2fcb 2f6b 2f2d 2f6e 2fee 2f23 2fef 2f2f 21e7e7 21e721 21e7cb
  //   21e76b 21e72d 21e76e 21e7ee 21e723 21e7ef 21e72f 2121e7 212121 2121cb 21216b 21212d 21216e 2121ee
  //   212123 2121ef 21212f 21cbe7 21cb21 21cbcb 21cb6b 21cb2d 21cb6e 21cbee 21cb23 21cbef 21cb2f 216be7
  //   216b21 216bcb 216b6b 216b2d 216b6e 216bee 216b23 216bef 216b2f 212de7 212d21 212dcb 212d6b 212d2d
  //   212d6e 212dee 212d23 212def 212d2f 216ee7 216e21 216ecb 216e6b 216e2d 216e6e 216eee 216e23 216eef
  //   216e2f 21eee7 21ee21 21eecb 21ee6b 21ee2d 21ee6e 21eeee 21ee23 21eeef 21ee2f 2123e7 212321 2123cb
  //   21236b 21232d 21236e 2123ee 212323 2123ef 21232f 21efe7 21ef21 21efcb 21ef6b 21ef2d 21ef6e 21efee
  //   21ef23 21efef 21ef2f 212fe7 212f21 212fcb 212f6b 212f2d 212f6e 212fee 212f23 212fef 212f2f cbe7e7
  //   cbe721 cbe7cb cbe76b cbe72d cbe76e cbe7ee cbe723 cbe7ef cbe72f cb21e7 cb2121 cb21cb cb216b cb212d
  //   cb216e cb21ee cb2123 cb21ef cb212f cbcbe7 cbcb21 cbcbcb cbcb6b cbcb2d cbcb6e cbcbee cbcb23 cbcbef
  //   cbcb2f cb6be7 cb6b21 cb6bcb cb6b6b cb6b2d cb6b6e cb6bee cb6b23 cb6bef cb6b2f cb2de7 cb2d21 cb2dcb
  //   cb2d6b cb2d2d cb2d6e cb2dee cb2d23 cb2def cb2d2f cb6ee7 cb6e21 cb6ecb cb6e6b cb6e2d cb6e6e
endmodule

module CU_1 (
  input  OPC3,
  input  OPC2,
  input  OPC1,
  input  OPC0,
  input  SC2,
  input  SC1,
  input  SC0,
  output C0,
  output C1,
  output C2,
  output C3,
  output C4,
  output C5,
  output C6,
  output C7,
  output C8,
  output C9,
  output C10,
  output C11
);

  wire and_4_out, and_5_out, and_6_out, and_7_out, and_8_out, and_9_out, and_10_out, and_13_out, and_14_out,
       and_15_out, and_16_out, and_17_out, and_18_out, and_19_out, and_20_out;

  and and_1 (C0, ~SC2, ~SC1, ~SC0);  // AND_Gate
  and and_2 (C1, ~SC2, ~SC1, SC0);  // AND_Gate
  and and_3 (C2, OPC1, OPC0, SC2, ~SC1, ~SC0);  // AND_Gate
  and and_4 (and_4_out, ~SC2, ~SC1, SC0);  // AND_Gate
  and and_5 (and_5_out, ~OPC1, SC2, ~SC1, ~SC0);  // AND_Gate
  and and_6 (and_6_out, ~SC2, ~SC1, SC0);  // AND_Gate
  and and_7 (and_7_out, ~OPC1, SC2, ~SC1, ~SC0);  // AND_Gate
  and and_8 (and_8_out, OPC1, OPC0, ~SC2, SC0);  // AND_Gate
  and and_9 (and_9_out, ~SC2, SC1, ~SC0);  // AND_Gate
  and and_10 (and_10_out, ~OPC1, SC2, ~SC1, SC0);  // AND_Gate
  and and_11 (C6, OPC1, OPC0, SC2, ~SC1, ~SC0);  // AND_Gate
  and and_12 (C7, ~SC2, SC1, ~SC0);  // AND_Gate
  and and_13 (and_13_out, ~OPC1, ~SC2, SC1, SC0);  // AND_Gate
  and and_14 (and_14_out, OPC0, ~SC2, SC1, SC0);  // AND_Gate
  and and_15 (and_15_out, ~SC2, ~SC1, ~SC0);  // AND_Gate
  and and_16 (and_16_out, ~OPC1, ~SC2, SC1, SC0);  // AND_Gate
  and and_17 (and_17_out, OPC0, ~SC2, SC1, SC0);  // AND_Gate
  and and_18 (and_18_out, ~SC2, ~SC1, SC0);  // AND_Gate
  and and_19 (and_19_out, ~OPC1, SC2, ~SC1, ~SC0);  // AND_Gate
  and and_20 (and_20_out, OPC0, SC2, ~SC1, ~SC0);  // AND_Gate
  and and_21 (C11, OPC1, ~OPC0, ~SC2, SC1, SC0);  // AND_Gate
  or or_1 (C3, and_4_out, and_5_out);
  or or_2 (C4, and_6_out, and_7_out, and_8_out);
  or or_3 (C5, and_9_out, and_10_out);
  or or_4 (C8, and_13_out, and_14_out);
  or or_5 (C9, and_15_out, and_16_out, and_17_out);
  or or_6 (C10, and_18_out, and_19_out, and_20_out);
endmodule

module CU_2 (
  input  OPC3,
  input  OPC2,
  input  OPC1,
  input  OPC0,
  input  SC2,
  input  SC1,
  input  SC0,
  output C12,
  output C13,
  output C14,
  output C15
);

  and and_1 (C12, ~OPC1, ~OPC0, SC2, ~SC1, SC0);  // AND_Gate
  and and_2 (C13, ~OPC1, OPC0, SC2, ~SC1, SC0);  // AND_Gate
  and and_3 (C14, OPC1, OPC0, ~SC2, SC1, SC0);  // AND_Gate
  and and_4 (C15, OPC1, ~OPC0, ~SC2, SC1, SC0);  // AND_Gate
endmodule

module manual_simulation (
  input  [3:0] in_1,
  input  OE,
  input  WE,
  input  [7:0] TD,
  input  CntrOE,
  input  OETD,
  input  CountE,
  input  Internal_OE,
  input  WE_2,
  input  WE_3,
  input  OE_2,
  input  OE_3,
  input  OE_4,
  input  WE_4,
  input  OE_5,
  input  WE_5,
  input  OE_6,
  input  WE_6,
  input  OE_7,
  input  OE_8,
  input  WE_7,
  input  OE_9,
  output [3:0] Cntr_Content,
  output [7:0] IR_Content,
  output [3:0] MAR_Content,
  output [7:0] MBR_Reg_Content,
  output [7:0] Reg_A_Content,
  output [7:0] ALU_Result,
  output [7:0] O_P_Reg_Content,
  output [7:0] Reg_B_Content
);

  wire clock_out;
  wire [3:0] controlled_buffer_1_out, decimal_decoer_2_dout_2, decimal_decoer_2_dout_3,
       decimal_decoer_3_dout_2, decimal_decoer_3_dout_3, decimal_decoer_4_dout_2, decimal_decoer_4_dout_3,
       mar_1_dout;
  wire [7:0] ALU_dout, bit_extender_1_out, decimal_decoer_2_dout, decimal_decoer_3_dout,
       decimal_decoer_4_dout, IR_dout, ram_1_dout;
  wire [15:0] decimal_decoer_2_dout_4, decimal_decoer_3_dout_4, decimal_decoer_4_dout_4;
  wire [31:0] decimal_decoer_1_dout;

  _7_Segment_Display u_7_segment_display_1 (
    .g(decimal_decoer_2_dout_3[3]), .f(decimal_decoer_2_dout_3[2]), .a(decimal_decoer_2_dout_3[1]),
    .b(decimal_decoer_2_dout_3[0]), .e(decimal_decoer_2_dout_4[15]), .d(decimal_decoer_2_dout_4[14]),
    .c(decimal_decoer_2_dout_4[13]), .dp(decimal_decoer_2_dout_4[12]));
  _7_Segment_Display u_7_segment_display_2 (
    .g(decimal_decoer_2_dout_2[3]), .f(decimal_decoer_2_dout_2[2]), .a(decimal_decoer_2_dout_2[1]),
    .b(decimal_decoer_2_dout_2[0]), .e(decimal_decoer_2_dout_4[11]), .d(decimal_decoer_2_dout_4[10]),
    .c(decimal_decoer_2_dout_4[9]), .dp(decimal_decoer_2_dout_4[8]));
  _7_Segment_Display u_7_segment_display_3 (
    .g(decimal_decoer_2_dout[7]), .f(decimal_decoer_2_dout[6]), .a(decimal_decoer_2_dout[5]),
    .b(decimal_decoer_2_dout[4]), .e(decimal_decoer_2_dout_4[7]), .d(decimal_decoer_2_dout_4[6]),
    .c(decimal_decoer_2_dout_4[5]), .dp(decimal_decoer_2_dout_4[4]));
  assign bit_extender_1_out = {{4{1'b0}}, Cntr_Content};  // Bit_Extender bit_extender_1
  Decimal_Decoer decimal_decoer_1 (.Din(bit_extender_1_out), .Dout(decimal_decoer_1_dout));
  _7_Segment_Display u_7_segment_display_4 (
    .g(decimal_decoer_1_dout[3]), .f(decimal_decoer_1_dout[2]), .a(decimal_decoer_1_dout[1]),
    .b(decimal_decoer_1_dout[0]), .e(decimal_decoer_1_dout[19]), .d(decimal_decoer_1_dout[18]),
    .c(decimal_decoer_1_dout[17]), .dp(decimal_decoer_1_dout[16]));
  Decimal_Decoer decimal_decoer_2 (
    .Din(Reg_A_Content),
    .Dout({decimal_decoer_2_dout_4, decimal_decoer_2_dout_3, decimal_decoer_2_dout_2, decimal_decoer_2_dout}));
  _7_Segment_Display u_7_segment_display_5 (
    .g(decimal_decoer_2_dout[3]), .f(decimal_decoer_2_dout[2]), .a(decimal_decoer_2_dout[1]),
    .b(decimal_decoer_2_dout[0]), .e(decimal_decoer_2_dout_4[3]), .d(decimal_decoer_2_dout_4[2]),
    .c(decimal_decoer_2_dout_4[1]), .dp(decimal_decoer_2_dout_4[0]));
  Clock clock (.out(clock_out));
  Counter #(.max('h3), .width(4)) PC (
    .D(controlled_buffer_1_out), .count(CountE), .Q(Cntr_Content), .clk(clock_out));  // open: load, carry, clr
  Register IR (.clock(clock_out), .WE(WE_2), .Din(ALU_dout), .OE(OE_2), .Dout(IR_dout), .Stored_Data(IR_Content));
  Register Reg_A (.clock(clock_out), .WE(WE_5), .Din(ALU_dout), .OE(OE_6), .Stored_Data(Reg_A_Content));  // open: Dout
  ALU ALU (
    .OE(OE_8), .Reg_A(Reg_A_Content), .Reg_B(Reg_B_Content), .Dout(ALU_dout), .ALU_result(ALU_Result));  // open: Carry_out
  Register Reg_B (.clock(clock_out), .WE(WE_7), .Din(ALU_dout), .OE(OE_9), .Stored_Data(Reg_B_Content));  // open: Dout
  _7_Segment_Display u_7_segment_display_6 (
    .g(decimal_decoer_3_dout_3[3]), .f(decimal_decoer_3_dout_3[2]), .a(decimal_decoer_3_dout_3[1]),
    .b(decimal_decoer_3_dout_3[0]), .e(decimal_decoer_3_dout_4[15]), .d(decimal_decoer_3_dout_4[14]),
    .c(decimal_decoer_3_dout_4[13]), .dp(decimal_decoer_3_dout_4[12]));
  _7_Segment_Display u_7_segment_display_7 (
    .g(decimal_decoer_3_dout_2[3]), .f(decimal_decoer_3_dout_2[2]), .a(decimal_decoer_3_dout_2[1]),
    .b(decimal_decoer_3_dout_2[0]), .e(decimal_decoer_3_dout_4[11]), .d(decimal_decoer_3_dout_4[10]),
    .c(decimal_decoer_3_dout_4[9]), .dp(decimal_decoer_3_dout_4[8]));
  assign controlled_buffer_1_out = CntrOE ? Cntr_Content : 4'bz;  // Controlled_Buffer controlled_buffer_1
  Decimal_Decoer decimal_decoer_3 (
    .Din(Reg_B_Content),
    .Dout({decimal_decoer_3_dout_4, decimal_decoer_3_dout_3, decimal_decoer_3_dout_2, decimal_decoer_3_dout}));
  _7_Segment_Display u_7_segment_display_8 (
    .g(decimal_decoer_3_dout[7]), .f(decimal_decoer_3_dout[6]), .a(decimal_decoer_3_dout[5]),
    .b(decimal_decoer_3_dout[4]), .e(decimal_decoer_3_dout_4[7]), .d(decimal_decoer_3_dout_4[6]),
    .c(decimal_decoer_3_dout_4[5]), .dp(decimal_decoer_3_dout_4[4]));
  _7_Segment_Display u_7_segment_display_9 (
    .g(decimal_decoer_3_dout[3]), .f(decimal_decoer_3_dout[2]), .a(decimal_decoer_3_dout[1]),
    .b(decimal_decoer_3_dout[0]), .e(decimal_decoer_3_dout_4[3]), .d(decimal_decoer_3_dout_4[2]),
    .c(decimal_decoer_3_dout_4[1]), .dp(decimal_decoer_3_dout_4[0]));
  BitSelector #(.group(4)) bitselector_1 (.in(IR_dout), .out(controlled_buffer_1_out), .sel(1'b0));
  LED D7 (.in(ALU_dout[7]));
  assign ALU_dout = OETD ? TD : 8'bz;  // Controlled_Buffer controlled_buffer_2
  LED D6 (.in(ALU_dout[6]));
  LED D5 (.in(ALU_dout[5]));
  LED D4 (.in(ALU_dout[4]));
  LED D3 (.in(ALU_dout[3]));
  assign ALU_dout = Internal_OE ? MBR_Reg_Content : 8'bz;  // Controlled_Buffer controlled_buffer_3
  _7_Segment_Display u_7_segment_display_10 (
    .g(decimal_decoer_4_dout_3[3]), .f(decimal_decoer_4_dout_3[2]), .a(decimal_decoer_4_dout_3[1]),
    .b(decimal_decoer_4_dout_3[0]), .e(decimal_decoer_4_dout_4[15]), .d(decimal_decoer_4_dout_4[14]),
    .c(decimal_decoer_4_dout_4[13]), .dp(decimal_decoer_4_dout_4[12]));
  LED D2 (.in(ALU_dout[2]));
  LED D1 (.in(ALU_dout[1]));
  LED D0 (.in(ALU_dout[0]));
  _7_Segment_Display u_7_segment_display_11 (
    .g(decimal_decoer_4_dout_2[3]), .f(decimal_decoer_4_dout_2[2]), .a(decimal_decoer_4_dout_2[1]),
    .b(decimal_decoer_4_dout_2[0]), .e(decimal_decoer_4_dout_4[11]), .d(decimal_decoer_4_dout_4[10]),
    .c(decimal_decoer_4_dout_4[9]), .dp(decimal_decoer_4_dout_4[8]));
  _7_Segment_Display u_7_segment_display_12 (
    .g(decimal_decoer_4_dout[7]), .f(decimal_decoer_4_dout[6]), .a(decimal_decoer_4_dout[5]),
    .b(decimal_decoer_4_dout[4]), .e(decimal_decoer_4_dout_4[7]), .d(decimal_decoer_4_dout_4[6]),
    .c(decimal_decoer_4_dout_4[5]), .dp(decimal_decoer_4_dout_4[4]));
  MAR mar_1 (
    .clock(clock_out), .WE(WE_3), .Din(controlled_buffer_1_out), .OE(OE_3), .Dout(mar_1_dout),
    .Stored_Data(MAR_Content));
  Register MBR (
    .clock(clock_out), .WE(WE_4), .Din(ALU_dout), .OE(OE_5), .Dout(ALU_dout), .Stored_Data(MBR_Reg_Content));
  Register O_P_Reg (
    .clock(clock_out), .WE(WE_6), .Din(ALU_dout), .OE(OE_7), .Dout(ALU_dout), .Stored_Data(O_P_Reg_Content));
  Decimal_Decoer decimal_decoer_4 (
    .Din(O_P_Reg_Content),
    .Dout({decimal_decoer_4_dout_4, decimal_decoer_4_dout_3, decimal_decoer_4_dout_2, decimal_decoer_4_dout}));
  _7_Segment_Display u_7_segment_display_13 (
    .g(decimal_decoer_4_dout[3]), .f(decimal_decoer_4_dout[2]), .a(decimal_decoer_4_dout[1]),
    .b(decimal_decoer_4_dout[0]), .e(decimal_decoer_4_dout_4[3]), .d(decimal_decoer_4_dout_4[2]),
    .c(decimal_decoer_4_dout_4[1]), .dp(decimal_decoer_4_dout_4[0]));
  assign mar_1_dout = OE ? in_1 : 4'bz;  // Controlled_Buffer controlled_buffer_4
  LED D7_2 (.in(ALU_dout[7]));
  LED D6_2 (.in(ALU_dout[6]));
  LED D5_2 (.in(ALU_dout[5]));
  LED D4_2 (.in(ALU_dout[4]));
  LED D3_2 (.in(ALU_dout[3]));
  LED D2_2 (.in(ALU_dout[2]));
  RAM #(.addrWidth(4)) ram_1 (.addr(mar_1_dout), .we(WE), .clk(clock_out), .din(ALU_dout), .dout(ram_1_dout));
  LED D1_2 (.in(ALU_dout[1]));
  LED D0_2 (.in(ALU_dout[0]));
  assign ALU_dout = OE_4 ? ram_1_dout : 8'bz;  // Controlled_Buffer controlled_buffer_5

  // Notes on the sheet:
  //   OETD-OE Testing Data 
  //   TD-Testing Data 
  //   Internal Address Bus(4 bits)
  //   Internal Data Bus
  //   External 
  //   Address 
  //   Bus(4 bits)
  //   External Data Bus
endmodule

module CU3 (
  input  OPC3,
  input  OPC2,
  input  OPC1,
  input  OPC0,
  input  SC2,
  input  SC1,
  input  SC0,
  output C0,
  output C1,
  output C2,
  output C3,
  output C4,
  output C5,
  output C6,
  output C7,
  output C8,
  output C9,
  output C10,
  output C11
);

  wire and_4_out, and_5_out, and_6_out, and_7_out, and_8_out, and_9_out, and_10_out, and_13_out, and_14_out,
       and_15_out, and_16_out, and_17_out, and_18_out, and_19_out, and_20_out;

  and and_1 (C0, ~SC2, ~SC1, ~SC0);  // AND_Gate
  and and_2 (C1, ~SC2, ~SC1, SC0);  // AND_Gate
  and and_3 (C2, OPC1, OPC0, SC2, ~SC1, ~SC0);  // AND_Gate
  and and_4 (and_4_out, ~SC2, ~SC1, SC0);  // AND_Gate
  and and_5 (and_5_out, ~OPC1, SC2, ~SC1, ~SC0);  // AND_Gate
  and and_6 (and_6_out, ~SC2, ~SC1, SC0);  // AND_Gate
  and and_7 (and_7_out, ~OPC1, SC2, ~SC1, ~SC0);  // AND_Gate
  and and_8 (and_8_out, OPC1, OPC0, ~SC2, SC0);  // AND_Gate
  and and_9 (and_9_out, ~SC2, SC1, ~SC0);  // AND_Gate
  and and_10 (and_10_out, ~OPC1, SC2, ~SC1, SC0);  // AND_Gate
  and and_11 (C6, OPC1, OPC0, SC2, ~SC1, ~SC0);  // AND_Gate
  and and_12 (C7, ~SC2, SC1, ~SC0);  // AND_Gate
  and and_13 (and_13_out, ~OPC1, ~SC2, SC1, SC0);  // AND_Gate
  and and_14 (and_14_out, OPC0, ~SC2, SC1, SC0);  // AND_Gate
  and and_15 (and_15_out, ~SC2, ~SC1, ~SC0);  // AND_Gate
  and and_16 (and_16_out, ~OPC1, ~SC2, SC1, SC0);  // AND_Gate
  and and_17 (and_17_out, OPC0, ~SC2, SC1, SC0);  // AND_Gate
  and and_18 (and_18_out, ~SC2, ~SC1, SC0);  // AND_Gate
  and and_19 (and_19_out, ~OPC1, SC2, ~SC1, ~SC0);  // AND_Gate
  and and_20 (and_20_out, OPC0, SC2, ~SC1, ~SC0);  // AND_Gate
  and and_21 (C11, OPC1, ~OPC0, ~SC2, SC1, SC0);  // AND_Gate
  or or_1 (C3, and_4_out, and_5_out);
  or or_2 (C4, and_6_out, and_7_out, and_8_out);
  or or_3 (C5, and_9_out, and_10_out);
  or or_4 (C8, and_13_out, and_14_out);
  or or_5 (C9, and_15_out, and_16_out, and_17_out);
  or or_6 (C10, and_18_out, and_19_out, and_20_out);
endmodule

module CU4 (
  input  OPC3,
  input  OPC2,
  input  OPC1,
  input  OPC0,
  input  SC2,
  input  SC1,
  input  SC0,
  output C12,
  output C13,
  output C14,
  output C15
);

  and and_1 (C12, ~OPC1, ~OPC0, SC2, ~SC1, SC0);  // AND_Gate
  and and_2 (C13, ~OPC1, OPC0, SC2, ~SC1, SC0);  // AND_Gate
  and and_3 (C14, OPC1, OPC0, ~SC2, SC1, SC0);  // AND_Gate
  and and_4 (C15, OPC1, ~OPC0, ~SC2, SC1, SC0);  // AND_Gate
endmodule

module manual_simulation1 (
  input  [3:0] in_1,
  input  OE,
  input  [7:0] TD,
  input  OETD,
  output [3:0] Cntr_Content,
  output [7:0] IR_Content,
  output [3:0] MAR_Content,
  output [7:0] MBR_Reg_Content,
  output [7:0] Reg_A_Content,
  output [7:0] ALU_Result,
  output [7:0] O_P_Reg_Content,
  output [3:0] out_12,
  output [7:0] Reg_B_Content,
  output [2:0] SC_Content
);

  wire clock_out, cu3_1_c0, cu3_1_c1, cu3_1_c2, cu3_1_c3, cu3_1_c4, cu3_1_c5, cu3_1_c6, cu3_1_c7, cu3_1_c8,
       cu3_1_c9, cu3_1_c10, cu3_1_c11, cu4_1_c12, cu4_1_c13, cu4_1_c14, cu4_1_c15;
  wire [3:0] controlled_buffer_1_out, decimal_decoer_2_dout_2, decimal_decoer_2_dout_3,
       decimal_decoer_3_dout_2, decimal_decoer_3_dout_3, decimal_decoer_4_dout_2, decimal_decoer_4_dout_3,
       decimal_decoer_5_dout_2, mar_1_dout;
  wire [7:0] ALU_dout, bit_extender_1_out, bit_extender_2_out, decimal_decoer_2_dout, decimal_decoer_3_dout,
       IR_dout, ram_1_dout;
  wire [11:0] decimal_decoer_5_dout;
  wire [15:0] decimal_decoer_2_dout_4, decimal_decoer_3_dout_4, decimal_decoer_4_dout,
       decimal_decoer_5_dout_3;
  wire [31:0] decimal_decoer_1_dout;
  wire [31:24] decimal_decoer_4_dout_4;

  _7_Segment_Display u_7_segment_display_1 (
    .g(decimal_decoer_2_dout_3[3]), .f(decimal_decoer_2_dout_3[2]), .a(decimal_decoer_2_dout_3[1]),
    .b(decimal_decoer_2_dout_3[0]), .e(decimal_decoer_2_dout_4[15]), .d(decimal_decoer_2_dout_4[14]),
    .c(decimal_decoer_2_dout_4[13]), .dp(decimal_decoer_2_dout_4[12]));
  _7_Segment_Display u_7_segment_display_2 (
    .g(decimal_decoer_2_dout_2[3]), .f(decimal_decoer_2_dout_2[2]), .a(decimal_decoer_2_dout_2[1]),
    .b(decimal_decoer_2_dout_2[0]), .e(decimal_decoer_2_dout_4[11]), .d(decimal_decoer_2_dout_4[10]),
    .c(decimal_decoer_2_dout_4[9]), .dp(decimal_decoer_2_dout_4[8]));
  _7_Segment_Display u_7_segment_display_3 (
    .g(decimal_decoer_2_dout[7]), .f(decimal_decoer_2_dout[6]), .a(decimal_decoer_2_dout[5]),
    .b(decimal_decoer_2_dout[4]), .e(decimal_decoer_2_dout_4[7]), .d(decimal_decoer_2_dout_4[6]),
    .c(decimal_decoer_2_dout_4[5]), .dp(decimal_decoer_2_dout_4[4]));
  assign bit_extender_1_out = {{4{1'b0}}, Cntr_Content};  // Bit_Extender bit_extender_1
  Decimal_Decoer decimal_decoer_1 (.Din(bit_extender_1_out), .Dout(decimal_decoer_1_dout));
  _7_Segment_Display u_7_segment_display_4 (
    .g(decimal_decoer_1_dout[3]), .f(decimal_decoer_1_dout[2]), .a(decimal_decoer_1_dout[1]),
    .b(decimal_decoer_1_dout[0]), .e(decimal_decoer_1_dout[19]), .d(decimal_decoer_1_dout[18]),
    .c(decimal_decoer_1_dout[17]), .dp(decimal_decoer_1_dout[16]));
  Decimal_Decoer decimal_decoer_2 (
    .Din(Reg_A_Content),
    .Dout({decimal_decoer_2_dout_4, decimal_decoer_2_dout_3, decimal_decoer_2_dout_2, decimal_decoer_2_dout}));
  _7_Segment_Display u_7_segment_display_5 (
    .g(decimal_decoer_2_dout[3]), .f(decimal_decoer_2_dout[2]), .a(decimal_decoer_2_dout[1]),
    .b(decimal_decoer_2_dout[0]), .e(decimal_decoer_2_dout_4[3]), .d(decimal_decoer_2_dout_4[2]),
    .c(decimal_decoer_2_dout_4[1]), .dp(decimal_decoer_2_dout_4[0]));
  Clock clock (.out(clock_out));
  Counter #(.max('h3), .width(4)) PC (
    .D(controlled_buffer_1_out), .count(cu3_1_c1), .Q(Cntr_Content), .clk(clock_out));  // open: load, carry, clr
  Register IR (
    .clock(clock_out), .WE(cu3_1_c7), .Din(ALU_dout), .OE(cu3_1_c8), .Dout(IR_dout), .Stored_Data(IR_Content));
  Register Reg_A (.clock(clock_out), .WE(cu4_1_c12), .Din(ALU_dout), .Stored_Data(Reg_A_Content));  // open: OE, Dout
  ALU ALU (
    .OE(cu3_1_c11), .Reg_A(Reg_A_Content), .Reg_B(Reg_B_Content), .Dout(ALU_dout), .ALU_result(ALU_Result));  // open: Carry_out
  Register Reg_B (.clock(clock_out), .WE(cu4_1_c13), .Din(ALU_dout), .Stored_Data(Reg_B_Content));  // open: OE, Dout
  _7_Segment_Display u_7_segment_display_6 (
    .g(decimal_decoer_3_dout_3[3]), .f(decimal_decoer_3_dout_3[2]), .a(decimal_decoer_3_dout_3[1]),
    .b(decimal_decoer_3_dout_3[0]), .e(decimal_decoer_3_dout_4[15]), .d(decimal_decoer_3_dout_4[14]),
    .c(decimal_decoer_3_dout_4[13]), .dp(decimal_decoer_3_dout_4[12]));
  _7_Segment_Display u_7_segment_display_7 (
    .g(decimal_decoer_3_dout_2[3]), .f(decimal_decoer_3_dout_2[2]), .a(decimal_decoer_3_dout_2[1]),
    .b(decimal_decoer_3_dout_2[0]), .e(decimal_decoer_3_dout_4[11]), .d(decimal_decoer_3_dout_4[10]),
    .c(decimal_decoer_3_dout_4[9]), .dp(decimal_decoer_3_dout_4[8]));
  assign controlled_buffer_1_out = cu3_1_c0 ? Cntr_Content : 4'bz;  // Controlled_Buffer controlled_buffer_1
  Decimal_Decoer decimal_decoer_3 (
    .Din(Reg_B_Content),
    .Dout({decimal_decoer_3_dout_4, decimal_decoer_3_dout_3, decimal_decoer_3_dout_2, decimal_decoer_3_dout}));
  _7_Segment_Display u_7_segment_display_8 (
    .g(decimal_decoer_3_dout[7]), .f(decimal_decoer_3_dout[6]), .a(decimal_decoer_3_dout[5]),
    .b(decimal_decoer_3_dout[4]), .e(decimal_decoer_3_dout_4[7]), .d(decimal_decoer_3_dout_4[6]),
    .c(decimal_decoer_3_dout_4[5]), .dp(decimal_decoer_3_dout_4[4]));
  _7_Segment_Display u_7_segment_display_9 (
    .g(decimal_decoer_3_dout[3]), .f(decimal_decoer_3_dout[2]), .a(decimal_decoer_3_dout[1]),
    .b(decimal_decoer_3_dout[0]), .e(decimal_decoer_3_dout_4[3]), .d(decimal_decoer_3_dout_4[2]),
    .c(decimal_decoer_3_dout_4[1]), .dp(decimal_decoer_3_dout_4[0]));
  BitSelector #(.group(4)) bitselector_1 (.in(IR_dout), .out(controlled_buffer_1_out), .sel(1'b0));
  LED D7 (.in(ALU_dout[7]));
  assign ALU_dout = OETD ? TD : 8'bz;  // Controlled_Buffer controlled_buffer_2
  LED D6 (.in(ALU_dout[6]));
  LED D5 (.in(ALU_dout[5]));
  LED D4 (.in(ALU_dout[4]));
  LED D3 (.in(ALU_dout[3]));
  assign ALU_dout = cu3_1_c5 ? MBR_Reg_Content : 8'bz;  // Controlled_Buffer controlled_buffer_3
  LED D2 (.in(ALU_dout[2]));
  LED D1 (.in(ALU_dout[1]));
  LED D0 (.in(ALU_dout[0]));
  _7_Segment_Display u_7_segment_display_10 (
    .g(decimal_decoer_4_dout[15]), .f(decimal_decoer_4_dout[14]), .a(decimal_decoer_4_dout[13]),
    .b(decimal_decoer_4_dout[12]), .e(decimal_decoer_4_dout_4[31]), .d(decimal_decoer_4_dout_4[30]),
    .c(decimal_decoer_4_dout_4[29]), .dp(decimal_decoer_4_dout_4[28]));
  MAR mar_1 (
    .clock(clock_out), .WE(cu3_1_c9), .Din(controlled_buffer_1_out), .OE(cu3_1_c10), .Dout(mar_1_dout),
    .Stored_Data(MAR_Content));
  Register MBR (
    .clock(clock_out), .WE(cu3_1_c4), .Din(ALU_dout), .OE(cu3_1_c6), .Dout(ALU_dout),
    .Stored_Data(MBR_Reg_Content));
  Register O_P_Reg (
    .clock(clock_out), .WE(cu4_1_c15), .Din(ALU_dout), .OE(cu4_1_c14), .Dout(ALU_dout),
    .Stored_Data(O_P_Reg_Content));
  Decimal_Decoer decimal_decoer_4 (
    .Din(O_P_Reg_Content),
    .Dout({decimal_decoer_4_dout_4, decimal_decoer_4_dout_3, decimal_decoer_4_dout_2, decimal_decoer_4_dout}));
  _7_Segment_Display u_7_segment_display_11 (
    .g(decimal_decoer_4_dout[7]), .f(decimal_decoer_4_dout[6]), .a(decimal_decoer_4_dout[5]),
    .b(decimal_decoer_4_dout[4]), .e(decimal_decoer_4_dout_3[3]), .d(decimal_decoer_4_dout_3[2]),
    .c(decimal_decoer_4_dout_3[1]), .dp(decimal_decoer_4_dout_3[0]));
  _7_Segment_Display u_7_segment_display_12 (
    .g(decimal_decoer_4_dout[11]), .f(decimal_decoer_4_dout[10]), .a(decimal_decoer_4_dout[9]),
    .b(decimal_decoer_4_dout[8]), .e(decimal_decoer_4_dout_4[27]), .d(decimal_decoer_4_dout_4[26]),
    .c(decimal_decoer_4_dout_4[25]), .dp(decimal_decoer_4_dout_4[24]));
  assign mar_1_dout = OE ? in_1 : 4'bz;  // Controlled_Buffer controlled_buffer_4
  _7_Segment_Display u_7_segment_display_13 (
    .g(decimal_decoer_4_dout[3]), .f(decimal_decoer_4_dout[2]), .a(decimal_decoer_4_dout[1]),
    .b(decimal_decoer_4_dout[0]), .e(decimal_decoer_4_dout_2[3]), .d(decimal_decoer_4_dout_2[2]),
    .c(decimal_decoer_4_dout_2[1]), .dp(decimal_decoer_4_dout_2[0]));
  LED D7_2 (.in(ALU_dout[7]));
  LED D6_2 (.in(ALU_dout[6]));
  LED D5_2 (.in(ALU_dout[5]));
  LED D4_2 (.in(ALU_dout[4]));
  LED D3_2 (.in(ALU_dout[3]));
  LED D2_2 (.in(ALU_dout[2]));
  RAM #(.addrWidth(4)) ram_1 (.addr(mar_1_dout), .we(cu3_1_c2), .clk(clock_out), .din(ALU_dout), .dout(ram_1_dout));
  BitSelector #(.group(4)) bitselector_2 (.in(Reg_A_Content), .out(out_12), .sel(1'b0));
  LED D1_2 (.in(ALU_dout[1]));
  LED D0_2 (.in(ALU_dout[0]));
  Counter #(.max('h5), .width(3)) PC_2 (.Q(SC_Content), .clk(clock_out));  // open: load, D, count, carry, clr
  assign ALU_dout = cu3_1_c3 ? ram_1_dout : 8'bz;  // Controlled_Buffer controlled_buffer_5
  assign bit_extender_2_out = {{5{1'b0}}, SC_Content};  // Bit_Extender bit_extender_2
  CU3 cu3_1 (
    .OPC3(out_12[3]), .OPC2(out_12[2]), .OPC1(out_12[1]), .OPC0(out_12[0]), .SC2(SC_Content[2]),
    .SC1(SC_Content[1]), .SC0(SC_Content[0]), .C0(cu3_1_c0), .C1(cu3_1_c1), .C2(cu3_1_c2), .C3(cu3_1_c3),
    .C4(cu3_1_c4), .C5(cu3_1_c5), .C6(cu3_1_c6), .C7(cu3_1_c7), .C8(cu3_1_c8), .C9(cu3_1_c9),
    .C10(cu3_1_c10), .C11(cu3_1_c11));
  CU4 cu4_1 (
    .OPC3(out_12[3]), .OPC2(out_12[2]), .OPC1(out_12[1]), .OPC0(out_12[0]), .SC2(SC_Content[2]),
    .SC1(SC_Content[1]), .SC0(SC_Content[0]), .C12(cu4_1_c12), .C13(cu4_1_c13), .C14(cu4_1_c14),
    .C15(cu4_1_c15));
  Decimal_Decoer decimal_decoer_5 (
    .Din(bit_extender_2_out), .Dout({decimal_decoer_5_dout_3, decimal_decoer_5_dout_2, decimal_decoer_5_dout}));
  _7_Segment_Display u_7_segment_display_14 (
    .g(decimal_decoer_5_dout[3]), .f(decimal_decoer_5_dout[2]), .a(decimal_decoer_5_dout[1]),
    .b(decimal_decoer_5_dout[0]), .e(decimal_decoer_5_dout_3[3]), .d(decimal_decoer_5_dout_3[2]),
    .c(decimal_decoer_5_dout_3[1]), .dp(decimal_decoer_5_dout_3[0]));

  // Notes on the sheet:
  //   TD-Testing Data 
  //   OETD-OE Testing Data 
  //   Internal Address Bus(4 bits)
  //   Internal Data Bus
  //   External 
  //   Address 
  //   Bus(4 bits)
  //   External Data Bus
endmodule

module manual_simulation2 (
  input  [3:0] in_1,
  input  OE,
  input  WE,
  input  [7:0] TD,
  input  CntrOE,
  input  OETD,
  input  CountE,
  input  Internal_OE,
  input  WE_2,
  input  WE_3,
  input  OE_2,
  input  OE_3,
  input  OE_4,
  input  WE_4,
  input  OE_5,
  input  WE_5,
  input  OE_6,
  input  WE_6,
  input  OE_7,
  input  OE_8,
  input  WE_7,
  input  OE_9,
  input  OETD_2,
  input  [7:0] TD_2,
  output [3:0] Cntr_Content,
  output [7:0] IR_Content,
  output [3:0] MAR_Content,
  output [7:0] MBR_Reg_Content,
  output [7:0] Reg_A_Content,
  output [7:0] ALU_Result,
  output [7:0] O_P_Reg_Content,
  output [7:0] Reg_B_Content
);

  wire clock_out;
  wire [3:0] controlled_buffer_1_out, decimal_decoer_2_dout_2, decimal_decoer_2_dout_3,
       decimal_decoer_3_dout_2, decimal_decoer_3_dout_3, decimal_decoer_4_dout_2, decimal_decoer_4_dout_3,
       mar_1_dout;
  wire [7:0] ALU_dout, bit_extender_1_out, decimal_decoer_2_dout, decimal_decoer_3_dout,
       decimal_decoer_4_dout, IR_dout, ram_1_dout;
  wire [15:0] decimal_decoer_2_dout_4, decimal_decoer_3_dout_4, decimal_decoer_4_dout_4;
  wire [31:0] decimal_decoer_1_dout;

  _7_Segment_Display u_7_segment_display_1 (
    .g(decimal_decoer_2_dout_3[3]), .f(decimal_decoer_2_dout_3[2]), .a(decimal_decoer_2_dout_3[1]),
    .b(decimal_decoer_2_dout_3[0]), .e(decimal_decoer_2_dout_4[15]), .d(decimal_decoer_2_dout_4[14]),
    .c(decimal_decoer_2_dout_4[13]), .dp(decimal_decoer_2_dout_4[12]));
  _7_Segment_Display u_7_segment_display_2 (
    .g(decimal_decoer_2_dout_2[3]), .f(decimal_decoer_2_dout_2[2]), .a(decimal_decoer_2_dout_2[1]),
    .b(decimal_decoer_2_dout_2[0]), .e(decimal_decoer_2_dout_4[11]), .d(decimal_decoer_2_dout_4[10]),
    .c(decimal_decoer_2_dout_4[9]), .dp(decimal_decoer_2_dout_4[8]));
  _7_Segment_Display u_7_segment_display_3 (
    .g(decimal_decoer_2_dout[7]), .f(decimal_decoer_2_dout[6]), .a(decimal_decoer_2_dout[5]),
    .b(decimal_decoer_2_dout[4]), .e(decimal_decoer_2_dout_4[7]), .d(decimal_decoer_2_dout_4[6]),
    .c(decimal_decoer_2_dout_4[5]), .dp(decimal_decoer_2_dout_4[4]));
  assign bit_extender_1_out = {{4{1'b0}}, Cntr_Content};  // Bit_Extender bit_extender_1
  Decimal_Decoer decimal_decoer_1 (.Din(bit_extender_1_out), .Dout(decimal_decoer_1_dout));
  _7_Segment_Display u_7_segment_display_4 (
    .g(decimal_decoer_1_dout[3]), .f(decimal_decoer_1_dout[2]), .a(decimal_decoer_1_dout[1]),
    .b(decimal_decoer_1_dout[0]), .e(decimal_decoer_1_dout[19]), .d(decimal_decoer_1_dout[18]),
    .c(decimal_decoer_1_dout[17]), .dp(decimal_decoer_1_dout[16]));
  Decimal_Decoer decimal_decoer_2 (
    .Din(Reg_A_Content),
    .Dout({decimal_decoer_2_dout_4, decimal_decoer_2_dout_3, decimal_decoer_2_dout_2, decimal_decoer_2_dout}));
  _7_Segment_Display u_7_segment_display_5 (
    .g(decimal_decoer_2_dout[3]), .f(decimal_decoer_2_dout[2]), .a(decimal_decoer_2_dout[1]),
    .b(decimal_decoer_2_dout[0]), .e(decimal_decoer_2_dout_4[3]), .d(decimal_decoer_2_dout_4[2]),
    .c(decimal_decoer_2_dout_4[1]), .dp(decimal_decoer_2_dout_4[0]));
  Clock clock (.out(clock_out));
  Counter #(.max('h3), .width(4)) PC (
    .D(controlled_buffer_1_out), .count(CountE), .Q(Cntr_Content), .clk(clock_out));  // open: load, carry, clr
  Register IR (.clock(clock_out), .WE(WE_2), .Din(ALU_dout), .OE(OE_2), .Dout(IR_dout), .Stored_Data(IR_Content));
  Register Reg_A (.clock(clock_out), .WE(WE_5), .Din(ALU_dout), .OE(OE_6), .Stored_Data(Reg_A_Content));  // open: Dout
  ALU ALU (
    .OE(OE_8), .Reg_A(Reg_A_Content), .Reg_B(Reg_B_Content), .Dout(ALU_dout), .ALU_result(ALU_Result));  // open: Carry_out
  Register Reg_B (.clock(clock_out), .WE(WE_7), .Din(ALU_dout), .OE(OE_9), .Stored_Data(Reg_B_Content));  // open: Dout
  _7_Segment_Display u_7_segment_display_6 (
    .g(decimal_decoer_3_dout_3[3]), .f(decimal_decoer_3_dout_3[2]), .a(decimal_decoer_3_dout_3[1]),
    .b(decimal_decoer_3_dout_3[0]), .e(decimal_decoer_3_dout_4[15]), .d(decimal_decoer_3_dout_4[14]),
    .c(decimal_decoer_3_dout_4[13]), .dp(decimal_decoer_3_dout_4[12]));
  _7_Segment_Display u_7_segment_display_7 (
    .g(decimal_decoer_3_dout_2[3]), .f(decimal_decoer_3_dout_2[2]), .a(decimal_decoer_3_dout_2[1]),
    .b(decimal_decoer_3_dout_2[0]), .e(decimal_decoer_3_dout_4[11]), .d(decimal_decoer_3_dout_4[10]),
    .c(decimal_decoer_3_dout_4[9]), .dp(decimal_decoer_3_dout_4[8]));
  assign controlled_buffer_1_out = CntrOE ? Cntr_Content : 4'bz;  // Controlled_Buffer controlled_buffer_1
  Decimal_Decoer decimal_decoer_3 (
    .Din(Reg_B_Content),
    .Dout({decimal_decoer_3_dout_4, decimal_decoer_3_dout_3, decimal_decoer_3_dout_2, decimal_decoer_3_dout}));
  _7_Segment_Display u_7_segment_display_8 (
    .g(decimal_decoer_3_dout[7]), .f(decimal_decoer_3_dout[6]), .a(decimal_decoer_3_dout[5]),
    .b(decimal_decoer_3_dout[4]), .e(decimal_decoer_3_dout_4[7]), .d(decimal_decoer_3_dout_4[6]),
    .c(decimal_decoer_3_dout_4[5]), .dp(decimal_decoer_3_dout_4[4]));
  _7_Segment_Display u_7_segment_display_9 (
    .g(decimal_decoer_3_dout[3]), .f(decimal_decoer_3_dout[2]), .a(decimal_decoer_3_dout[1]),
    .b(decimal_decoer_3_dout[0]), .e(decimal_decoer_3_dout_4[3]), .d(decimal_decoer_3_dout_4[2]),
    .c(decimal_decoer_3_dout_4[1]), .dp(decimal_decoer_3_dout_4[0]));
  BitSelector #(.group(4)) bitselector_1 (.in(IR_dout), .out(controlled_buffer_1_out), .sel(1'b0));
  assign ALU_dout = OETD ? TD : 8'bz;  // Controlled_Buffer controlled_buffer_2
  assign ALU_dout = OETD_2 ? TD_2 : 8'bz;  // Controlled_Buffer controlled_buffer_3
  assign ALU_dout = Internal_OE ? MBR_Reg_Content : 8'bz;  // Controlled_Buffer controlled_buffer_4
  _7_Segment_Display u_7_segment_display_10 (
    .g(decimal_decoer_4_dout_3[3]), .f(decimal_decoer_4_dout_3[2]), .a(decimal_decoer_4_dout_3[1]),
    .b(decimal_decoer_4_dout_3[0]), .e(decimal_decoer_4_dout_4[15]), .d(decimal_decoer_4_dout_4[14]),
    .c(decimal_decoer_4_dout_4[13]), .dp(decimal_decoer_4_dout_4[12]));
  _7_Segment_Display u_7_segment_display_11 (
    .g(decimal_decoer_4_dout_2[3]), .f(decimal_decoer_4_dout_2[2]), .a(decimal_decoer_4_dout_2[1]),
    .b(decimal_decoer_4_dout_2[0]), .e(decimal_decoer_4_dout_4[11]), .d(decimal_decoer_4_dout_4[10]),
    .c(decimal_decoer_4_dout_4[9]), .dp(decimal_decoer_4_dout_4[8]));
  _7_Segment_Display u_7_segment_display_12 (
    .g(decimal_decoer_4_dout[7]), .f(decimal_decoer_4_dout[6]), .a(decimal_decoer_4_dout[5]),
    .b(decimal_decoer_4_dout[4]), .e(decimal_decoer_4_dout_4[7]), .d(decimal_decoer_4_dout_4[6]),
    .c(decimal_decoer_4_dout_4[5]), .dp(decimal_decoer_4_dout_4[4]));
  MAR mar_1 (
    .clock(clock_out), .WE(WE_3), .Din(controlled_buffer_1_out), .OE(OE_3), .Dout(mar_1_dout),
    .Stored_Data(MAR_Content));
  Register MBR (
    .clock(clock_out), .WE(WE_4), .Din(ALU_dout), .OE(OE_5), .Dout(ALU_dout), .Stored_Data(MBR_Reg_Content));
  Register O_P_Reg (
    .clock(clock_out), .WE(WE_6), .Din(ALU_dout), .OE(OE_7), .Dout(ALU_dout), .Stored_Data(O_P_Reg_Content));
  Decimal_Decoer decimal_decoer_4 (
    .Din(O_P_Reg_Content),
    .Dout({decimal_decoer_4_dout_4, decimal_decoer_4_dout_3, decimal_decoer_4_dout_2, decimal_decoer_4_dout}));
  _7_Segment_Display u_7_segment_display_13 (
    .g(decimal_decoer_4_dout[3]), .f(decimal_decoer_4_dout[2]), .a(decimal_decoer_4_dout[1]),
    .b(decimal_decoer_4_dout[0]), .e(decimal_decoer_4_dout_4[3]), .d(decimal_decoer_4_dout_4[2]),
    .c(decimal_decoer_4_dout_4[1]), .dp(decimal_decoer_4_dout_4[0]));
  assign mar_1_dout = OE ? in_1 : 4'bz;  // Controlled_Buffer controlled_buffer_5
  LED D7 (.in(ALU_dout[7]));
  LED D6 (.in(ALU_dout[6]));
  LED D5 (.in(ALU_dout[5]));
  LED D4 (.in(ALU_dout[4]));
  LED D3 (.in(ALU_dout[3]));
  LED D2 (.in(ALU_dout[2]));
  RAM #(.addrWidth(4)) ram_1 (.addr(mar_1_dout), .we(WE), .clk(clock_out), .din(ALU_dout), .dout(ram_1_dout));
  LED D1 (.in(ALU_dout[1]));
  LED D0 (.in(ALU_dout[0]));
  assign ALU_dout = OE_4 ? ram_1_dout : 8'bz;  // Controlled_Buffer controlled_buffer_6

  // Notes on the sheet:
  //   OETD-OE Testing Data 
  //   TD-Testing Data 
  //   Internal Address Bus(4 bits)
  //   Internal Data Bus
  //   External 
  //   Address 
  //   Bus(4 bits)
  //   External Data Bus
endmodule
